// Logisim project MipsProcessor.circ as structural Verilog: 31 circuits, main circuit DecodingLogic
module MIPS32 (
  input  Panic
);

  wire Clock_out, datahazdetect_1_datahaz, EX_jump_2, ex_mem2_1_memread_2, ex_mem2_1_memsize_2,
       ex_mem2_1_memtoreg_2, ex_mem2_1_memwrite_2, EX_MEM_regwrite_2, EX_MEM_signed_2, EX_regwrite_2,
       EX_signed_2, id_ex2_1_jump_2, id_ex2_1_jumpreg_2, id_ex2_1_memread_2, id_ex2_1_memsize_2,
       id_ex2_1_memtoreg_2, id_ex2_1_memwrite_2, id_ex2_1_retregadd_2, id_ex2_1_storereturn_2, ID_EX_obranch,
       ID_EX_ocomp, ID_EX_olui, ID_EX_omove, ID_EX_oregwrite, ID_EX_osigned, ID_EX_osignext, ID_EX_ouseimm,
       ID_EX_ovs, ID_EX_stall_2, ID_jump, ID_jumpreg, ID_memread, ID_memsize, ID_memtoreg, ID_memwrite,
       ID_obranch, ID_ocomp, ID_olui, ID_omove, ID_osigned, ID_osignext, ID_ovs, ID_regwrite, ID_retregadd,
       ID_storereturn, ID_useimm, MEM_regwrite_2, Not_Implemented_stall, registerfile_1_p1;
  wire [1:0] forwardexmem_1_forward, forwardexmem_2_forward;
  wire [2:0] ID_compop, ID_EX_ocompop;
  wire [3:0] ID_aluop, ID_EX_aluop_2;
  wire [4:0] EX_addressrd_2, EX_MEM_rdaddress_2, ID_EX_addra, ID_EX_addrb, ID_EX_addressrdout, ID_EX_saout,
       ID_ra, ID_rb, ID_rd, ID_sa, MEM_rdaddress_2, registerfile_1_p2, undriven;
  wire [15:0] ID_EX_immout, ID_imm;
  wire [25:0] ID_EX_ins_index_2, ID_instr_index;
  wire [31:0] delayslot_1_instruction_2, EX_jumpaddress, EX_MEM_jumpaddress_2, EX_MEM_outputtostoreregout,
       EX_MEM_pc_4_2, EX_MEM_rt_2, EX_outputtostorereg, EX_pc_4_2, EX_rt_2, ID_EX_pc_4_2, ID_EX_rsout,
       ID_EX_rtout, ID_instruction_2, ID_pc_4_2, IF_ID_insout, IF_ID_pc_4out, MEM_outputtostoreregout,
       MEM_pc_4_2, mipsprogramrom_1_p2, mipsprogramrom_1_p3, multiplexer_1_out, pcplus4_1_pcplus4,
       register_1_q, registerfile_1_p5, registerfile_1_p6;

  Clock Clock (.out(Clock_out));
  Multiplexer #(.width(32), .enable("false")) multiplexer_1 (
    .in0(pcplus4_1_pcplus4), .in1(EX_jumpaddress), .out(multiplexer_1_out), .sel(EX_jump_2));
  Register #(.width(32)) register_1 (
    .D(multiplexer_1_out), .Q(register_1_q), .clk(Clock_out), .clr(Panic));  // open: en
  PCPlus4 pcplus4_1 (.PC(register_1_q), .PCplus4(pcplus4_1_pcplus4));
  IF_ID IF_ID (
    .Instruction(mipsprogramrom_1_p2), .PC_4(pcplus4_1_pcplus4), .Clock(Clock_out), .Panic(Panic),
    .InsOut(IF_ID_insout), .PC_4Out(IF_ID_pc_4out));
  // MIPSProgramROM mipsprogramrom_1: pin names not known; wires that end beside it: register_1_q, mipsprogramrom_1_p2, mipsprogramrom_1_p3, Clock_out
  ID ID (
    .Instruction(IF_ID_insout), .PC_4(IF_ID_pc_4out), .RegWrite(ID_regwrite), .UseImm(ID_useimm),
    .ALUOp(ID_aluop), .OSignExt(ID_osignext), .OMove(ID_omove), .OVS(ID_ovs), .CompOp(ID_compop),
    .OSigned(ID_osigned), .OComp(ID_ocomp), .OLui(ID_olui), .OBranch(ID_obranch), .Ra(ID_ra), .Rb(ID_rb),
    .SA(ID_sa), .Imm(ID_imm), .Rd(ID_rd), .PC_4_2(ID_pc_4_2), .Instr_Index(ID_instr_index),
    .Instruction_2(ID_instruction_2), .MemRead(ID_memread), .MemWrite(ID_memwrite), .JumpReg(ID_jumpreg),
    .MemToReg(ID_memtoreg), .RetRegAdd(ID_retregadd), .StoreReturn(ID_storereturn), .MemSize(ID_memsize),
    .Jump(ID_jump));
  DelaySlot delayslot_1 (.Instruction(ID_instruction_2), .Instruction_2(delayslot_1_instruction_2));
  StallChecker Not_Implemented (.Stall(Not_Implemented_stall));  // open: ID_EX_MemRead, IF_ID_Rs, ID_EX_Rt, IF_ID_Rt
  // RegisterFile registerfile_1: pin names not known; wires that end beside it: registerfile_1_p1, registerfile_1_p2, ID_ra, ID_rb, registerfile_1_p5, registerfile_1_p6
  ID_EX ID_EX (
    .AddressRa(ID_ra), .AddressRb(ID_rb), .RegWrite(ID_regwrite), .UseImm(ID_useimm), .ALUOp(ID_aluop),
    .SignExt(ID_osignext), .Move(ID_omove), .VS(ID_ovs), .CompOp(ID_compop), .Signed(ID_osigned),
    .Comp(ID_ocomp), .Lui(ID_olui), .Branch(ID_obranch), .Rs(registerfile_1_p5), .Rt(registerfile_1_p6),
    .SA(ID_sa), .Imm(ID_imm), .AddressRd(ID_rd), .PC_4(ID_pc_4_2), .Ins_Index(ID_instr_index),
    .Clock(Clock_out), .Reset(Panic), .Stall(Not_Implemented_stall), .AddRa(ID_EX_addra),
    .AddRb(ID_EX_addrb), .ORegWrite(ID_EX_oregwrite), .OUseImm(ID_EX_ouseimm), .ALUOp_2(ID_EX_aluop_2),
    .OSignExt(ID_EX_osignext), .OMove(ID_EX_omove), .OVS(ID_EX_ovs), .OCompOp(ID_EX_ocompop),
    .OSigned(ID_EX_osigned), .OComp(ID_EX_ocomp), .OLui(ID_EX_olui), .OBranch(ID_EX_obranch),
    .RsOut(ID_EX_rsout), .Rtout(ID_EX_rtout), .SAOut(ID_EX_saout), .ImmOut(ID_EX_immout),
    .AddressRdOut(ID_EX_addressrdout), .Stall_2(ID_EX_stall_2), .PC_4_2(ID_EX_pc_4_2),
    .Ins_Index_2(ID_EX_ins_index_2));
  ID_EX2 id_ex2_1 (
    .MemRead(ID_memread), .MemWrite(ID_memwrite), .JumpReg(ID_jumpreg), .MemToReg(ID_memtoreg),
    .RetRegAdd(ID_retregadd), .StoreReturn(ID_storereturn), .MemSize(ID_memsize), .Jump(ID_jump),
    .Clock(Clock_out), .Reset(Panic), .MemRead_2(id_ex2_1_memread_2), .MemWrite_2(id_ex2_1_memwrite_2),
    .JumpReg_2(id_ex2_1_jumpreg_2), .MemToReg_2(id_ex2_1_memtoreg_2), .RetRegAdd_2(id_ex2_1_retregadd_2),
    .StoreReturn_2(id_ex2_1_storereturn_2), .MemSize_2(id_ex2_1_memsize_2), .Jump_2(id_ex2_1_jump_2));
  // Probe on datahazdetect_1_datahaz
  DataHazDetect datahazdetect_1 (
    .Ra(ID_EX_addra), .IdEx(ID_EX_addressrdout), .Rb(ID_EX_addrb), .DataHaz(datahazdetect_1_datahaz),
    .ExMem(undriven), .MemWb(registerfile_1_p2));
  EX EX (
    .RegWrite(ID_EX_oregwrite), .UseImm(ID_EX_ouseimm), .ALUOp(ID_EX_aluop_2), .SignExt(ID_EX_osignext),
    .Move(ID_EX_omove), .VS(ID_EX_ovs), .CompOp(ID_EX_ocompop), .Signed(ID_EX_osigned), .Comp(ID_EX_ocomp),
    .Lui(ID_EX_olui), .Branch(ID_EX_obranch), .Rs(ID_EX_rsout), .Rt(ID_EX_rtout), .Sa(ID_EX_saout),
    .Imm(ID_EX_immout), .AddressRd(ID_EX_addressrdout), .Stall(ID_EX_stall_2), .PC_4(ID_EX_pc_4_2),
    .FwdA(forwardexmem_1_forward), .FwdB(forwardexmem_2_forward), .RegExMem(EX_MEM_outputtostoreregout),
    .RegMemWb(mipsprogramrom_1_p3), .JumpReg(id_ex2_1_jumpreg_2), .DelaySlot(delayslot_1_instruction_2),
    .Ins_Index(ID_EX_ins_index_2), .RetRegAddress(id_ex2_1_retregadd_2), .Jump(id_ex2_1_jump_2),
    .StoreReturn(id_ex2_1_storereturn_2), .JumpAddress(EX_jumpaddress), .RegWrite_2(EX_regwrite_2),
    .OutputToStoreReg(EX_outputtostorereg), .Signed_2(EX_signed_2), .AddressRd_2(EX_addressrd_2),
    .PC_4_2(EX_pc_4_2), .Rt_2(EX_rt_2), .Jump_2(EX_jump_2));
  EX_MEM EX_MEM (
    .JumpAddress(EX_jumpaddress), .RegWrite(EX_regwrite_2), .OutputToStoreReg(EX_outputtostorereg),
    .Signed(EX_signed_2), .RdAddress(EX_addressrd_2), .PC_4(EX_pc_4_2), .Rt(EX_rt_2), .Clock(Clock_out),
    .Reset(Panic), .JumpAddress_2(EX_MEM_jumpaddress_2), .RegWrite_2(EX_MEM_regwrite_2),
    .OutputToStoreRegOut(EX_MEM_outputtostoreregout), .Signed_2(EX_MEM_signed_2),
    .RdAddress_2(EX_MEM_rdaddress_2), .PC_4_2(EX_MEM_pc_4_2), .Rt_2(EX_MEM_rt_2));
  EX_MEM2 ex_mem2_1 (
    .MemToReg(id_ex2_1_memtoreg_2), .MemWrite(id_ex2_1_memwrite_2), .MemRead(id_ex2_1_memread_2),
    .MemSize(id_ex2_1_memsize_2), .Clock(Clock_out), .Reset(Panic), .MemToReg_2(ex_mem2_1_memtoreg_2),
    .MemWrite_2(ex_mem2_1_memwrite_2), .MemRead_2(ex_mem2_1_memread_2), .MemSize_2(ex_mem2_1_memsize_2));
  MEM MEM (
    .JumpAddress(EX_MEM_jumpaddress_2), .RegWrite(EX_MEM_regwrite_2),
    .OutputToStoreReg(EX_MEM_outputtostoreregout), .Signed(EX_MEM_signed_2), .RdAddress(EX_MEM_rdaddress_2),
    .PC_4(EX_MEM_pc_4_2), .Rt(EX_MEM_rt_2), .MemSize(ex_mem2_1_memsize_2), .MemRead(ex_mem2_1_memread_2),
    .MemWrite(ex_mem2_1_memwrite_2), .MemToReg(ex_mem2_1_memtoreg_2), .RegWrite_2(MEM_regwrite_2),
    .OutputToStoreRegOut(MEM_outputtostoreregout), .RdAddress_2(MEM_rdaddress_2), .PC_4_2(MEM_pc_4_2));
  ForwardExMem forwardexmem_1 (
    .WE(EX_MEM_regwrite_2), .Rd(undriven), .Ra_Rb(ID_EX_addra), .Forward(forwardexmem_1_forward[0]));
  ForwardExMem forwardexmem_2 (
    .WE(EX_MEM_regwrite_2), .Rd(undriven), .Ra_Rb(ID_EX_addrb), .Forward(forwardexmem_2_forward[0]));
  MEM_WB MEM_WB (
    .RegWrite(MEM_regwrite_2), .OutputToStoreReg(MEM_outputtostoreregout), .RdAddress(MEM_rdaddress_2),
    .PC_4(MEM_pc_4_2), .Clock(Clock_out), .Reset(Panic), .RegWrite_2(registerfile_1_p1),
    .OutputToStoreRegOut(mipsprogramrom_1_p3), .RdAddress_2(registerfile_1_p2));  // open: PC_4Out
  ForwardMemWb forwardmemwb_1 (
    .WE(registerfile_1_p1), .Rd(registerfile_1_p2), .Ra_Rb(ID_EX_addra), .WE0(EX_MEM_regwrite_2),
    .Rd0(undriven), .Forward(forwardexmem_1_forward[1]));
  ForwardMemWb forwardmemwb_2 (
    .WE(registerfile_1_p1), .Rd(registerfile_1_p2), .Ra_Rb(ID_EX_addrb), .WE0(EX_MEM_regwrite_2),
    .Rd0(undriven), .Forward(forwardexmem_2_forward[1]));
endmodule

module IF_ID (
  input  [31:0] Instruction,
  input  [31:0] PC_4,
  input  Clock,
  input  Panic,
  output [31:0] InsOut,
  output [31:0] PC_4Out
);

  Register #(.width(32)) register_1 (.D(Instruction), .Q(InsOut), .clk(Clock), .clr(Panic));  // open: en
  Register #(.width(32)) register_2 (.D(PC_4), .Q(PC_4Out), .clk(Clock), .clr(Panic));  // open: en
endmodule

module ID (
  input  [31:0] Instruction,
  input  [31:0] PC_4,
  output RegWrite,
  output UseImm,
  output [3:0] ALUOp,
  output OSignExt,
  output OMove,
  output OVS,
  output [2:0] CompOp,
  output OSigned,
  output OComp,
  output OLui,
  output OBranch,
  output [4:0] Ra,
  output [4:0] Rb,
  output [4:0] SA,
  output [15:0] Imm,
  output [4:0] Rd,
  output [31:0] PC_4_2,
  output [25:0] Instr_Index,
  output [31:0] Instruction_2,
  output MemRead,
  output MemWrite,
  output JumpReg,
  output MemToReg,
  output RetRegAdd,
  output StoreReturn,
  output MemSize,
  output Jump
);

  wire and_1_out, decodinglogic_1_regdst, decodingregimm_1_regimm;
  wire [5:0] multiplexer_1_out, not_1_out;

  assign not_1_out = ~Instruction[31:26];  // NOT_Gate not_1, 6 bits wide
  and and_1 (and_1_out, not_1_out[0], not_1_out[1], not_1_out[2], not_1_out[3], not_1_out[4], not_1_out[5]);
  Multiplexer #(.width(6), .enable("false")) multiplexer_1 (
    .in0(Instruction[31:26]), .in1(Instruction[5:0]), .out(multiplexer_1_out), .sel(and_1_out));
  DecodingLogicComp decodinglogiccomp_1 (
    .Bit5(multiplexer_1_out[5]), .Bit4(multiplexer_1_out[4]), .Bit3(multiplexer_1_out[3]),
    .Bit2(multiplexer_1_out[2]), .Bit1(multiplexer_1_out[1]), .Bit0(multiplexer_1_out[0]), .Rtype(and_1_out),
    .Comp2(CompOp[0]), .Comp1(CompOp[1]), .Comp0(CompOp[2]), .Signed(OSigned), .Comp(OComp));
  DecodingLogicLui decodinglogiclui_1 (
    .Bit5(multiplexer_1_out[5]), .Bit4(multiplexer_1_out[4]), .Bit3(multiplexer_1_out[3]),
    .Bit2(multiplexer_1_out[2]), .Bit1(multiplexer_1_out[1]), .Bit0(multiplexer_1_out[0]), .Rtype(and_1_out),
    .LUI(OLui));
  DecodingREGIMM decodingregimm_1 (
    .Bit5(multiplexer_1_out[5]), .Bit4(multiplexer_1_out[4]), .Bit3(multiplexer_1_out[3]),
    .Bit2(multiplexer_1_out[2]), .Bit1(multiplexer_1_out[1]), .Bit0(multiplexer_1_out[0]), .Rtype(and_1_out),
    .REGIMM(decodingregimm_1_regimm));
  DecodingMem_Jumps decodingmem_jumps_1 (
    .b5(multiplexer_1_out[5]), .b4(multiplexer_1_out[4]), .b3(multiplexer_1_out[3]),
    .b2(multiplexer_1_out[2]), .b1(multiplexer_1_out[1]), .b0(multiplexer_1_out[0]), .r(and_1_out),
    .MemRd(MemRead), .MemW(MemWrite), .JumpReg(JumpReg), .MemToReg(MemToReg), .RetRegAdd(RetRegAdd),
    .StoreRet(StoreReturn), .MemSize(MemSize), .Jump(Jump));
  DecodingLogic decodinglogic_1 (
    .Bit5(multiplexer_1_out[5]), .Bit4(multiplexer_1_out[4]), .Bit3(multiplexer_1_out[3]),
    .Bit2(multiplexer_1_out[2]), .Bit1(multiplexer_1_out[1]), .Bit0(multiplexer_1_out[0]), .Rtype(and_1_out),
    .RegDst(decodinglogic_1_regdst), .RegWrite(RegWrite), .ALUSrc(UseImm), .ALUOp3(ALUOp[3]),
    .ALUOp2(ALUOp[2]), .ALUOp1(ALUOp[1]), .ALUOp0(ALUOp[0]), .SignExt(OSignExt), .Move(OMove), .VS(OVS));
  DecodingLogicBranch decodinglogicbranch_1 (
    .Bit5(multiplexer_1_out[5]), .Bit4(multiplexer_1_out[4]), .Bit3(multiplexer_1_out[3]),
    .Bit2(multiplexer_1_out[2]), .Bit1(multiplexer_1_out[1]), .Bit0(multiplexer_1_out[0]), .Rtype(and_1_out),
    .REGIMM(decodingregimm_1_regimm), .Branch(OBranch));
  Multiplexer #(.width(5), .enable("false")) multiplexer_2 (
    .in0(Instruction[20:16]), .in1(Instruction[15:11]), .out(Rd), .sel(decodinglogic_1_regdst));

  assign Imm = Instruction[15:0];
  assign Instr_Index = Instruction[25:0];
  assign Instruction_2 = Instruction;
  assign PC_4_2 = PC_4;
  assign Ra = Instruction[25:21];
  assign Rb = Instruction[20:16];
  assign SA = Instruction[10:6];
endmodule

module ID_EX (
  input  [4:0] AddressRa,
  input  [4:0] AddressRb,
  input  RegWrite,
  input  UseImm,
  input  [3:0] ALUOp,
  input  SignExt,
  input  Move,
  input  VS,
  input  [2:0] CompOp,
  input  Signed,
  input  Comp,
  input  Lui,
  input  Branch,
  input  [31:0] Rs,
  input  [31:0] Rt,
  input  [4:0] SA,
  input  [15:0] Imm,
  input  [4:0] AddressRd,
  input  Stall,
  input  [31:0] PC_4,
  input  [25:0] Ins_Index,
  input  Clock,
  input  Reset,
  output [4:0] AddRa,
  output [4:0] AddRb,
  output ORegWrite,
  output OUseImm,
  output [3:0] ALUOp_2,
  output OSignExt,
  output OMove,
  output OVS,
  output [2:0] OCompOp,
  output OSigned,
  output OComp,
  output OLui,
  output OBranch,
  output [31:0] RsOut,
  output [31:0] Rtout,
  output [4:0] SAOut,
  output [15:0] ImmOut,
  output [4:0] AddressRdOut,
  output Stall_2,
  output [31:0] PC_4_2,
  output [25:0] Ins_Index_2
);

  Register #(.width(5)) register_1 (.D(AddressRa), .Q(AddRa), .clk(Clock), .clr(Reset));  // open: en
  Register #(.width(5)) register_2 (.D(AddressRb), .Q(AddRb), .clk(Clock), .clr(Reset));  // open: en
  Register #(.width(1)) register_3 (.D(RegWrite), .Q(ORegWrite), .clk(Clock), .clr(Reset));  // open: en
  Register #(.width(1)) register_4 (.D(UseImm), .Q(OUseImm), .clk(Clock), .clr(Reset));  // open: en
  Register #(.width(4)) register_5 (.D(ALUOp), .Q(ALUOp_2), .clk(Clock), .clr(Reset));  // open: en
  Register #(.width(1)) register_6 (.D(SignExt), .Q(OSignExt), .clk(Clock), .clr(Reset));  // open: en
  Register #(.width(1)) register_7 (.D(Move), .Q(OMove), .clk(Clock), .clr(Reset));  // open: en
  Register #(.width(1)) register_8 (.D(VS), .Q(OVS), .clk(Clock), .clr(Reset));  // open: en
  Register #(.width(3)) register_9 (.D(CompOp), .Q(OCompOp), .clk(Clock), .clr(Reset));  // open: en
  Register #(.width(1)) register_10 (.D(Signed), .Q(OSigned), .clk(Clock), .clr(Reset));  // open: en
  Register #(.width(1)) register_11 (.D(Comp), .Q(OComp), .clk(Clock), .clr(Reset));  // open: en
  Register #(.width(1)) register_12 (.D(Lui), .Q(OLui), .clk(Clock), .clr(Reset));  // open: en
  Register #(.width(1)) register_13 (.D(Branch), .Q(OBranch), .clk(Clock), .clr(Reset));  // open: en
  Register #(.width(32)) register_14 (.D(Rs), .Q(RsOut), .clk(Clock), .clr(Reset));  // open: en
  Register #(.width(32)) register_15 (.D(Rt), .Q(Rtout), .clk(Clock), .clr(Reset));  // open: en
  Register #(.width(5)) register_16 (.D(SA), .Q(SAOut), .clk(Clock), .clr(Reset));  // open: en
  Register #(.width(16)) register_17 (.D(Imm), .Q(ImmOut), .clk(Clock), .clr(Reset));  // open: en
  Register #(.width(5)) register_18 (.D(AddressRd), .Q(AddressRdOut), .clk(Clock), .clr(Reset));  // open: en
  Register #(.width(1)) register_19 (.D(Stall), .Q(Stall_2), .clk(Clock), .clr(Reset));  // open: en
  Register #(.width(32)) register_20 (.D(PC_4), .Q(PC_4_2), .clk(Clock), .clr(Reset));  // open: en
  Register #(.width(26)) register_21 (.D(Ins_Index), .Q(Ins_Index_2), .clk(Clock), .clr(Reset));  // open: en
endmodule

module EX (
  input  JumpReg,
  input  [31:0] DelaySlot,
  input  [1:0] FwdA,
  input  [31:0] RegExMem,
  input  [31:0] RegMemWb,
  input  [1:0] FwdB,
  input  RegWrite,
  input  UseImm,
  input  [3:0] ALUOp,
  input  SignExt,
  input  Move,
  input  VS,
  input  [2:0] CompOp,
  input  Signed,
  input  Comp,
  input  Lui,
  input  Branch,
  input  [31:0] Rs,
  input  [31:0] Rt,
  input  [4:0] Sa,
  input  [15:0] Imm,
  input  [4:0] AddressRd,
  input  Stall,
  input  [31:0] PC_4,
  input  RetRegAddress,
  input  Jump,
  input  StoreReturn,
  input  [25:0] Ins_Index,
  output [31:0] JumpAddress,
  output RegWrite_2,
  output [31:0] OutputToStoreReg,
  output Signed_2,
  output [4:0] AddressRd_2,
  output [31:0] PC_4_2,
  output [31:0] Rt_2,
  output Jump_2
);

  wire comparator_1_result, lastbit_1_out, multiplexer_11_out, not_1_out;
  wire [4:0] multiplexer_3_out, multiplexer_4_out;
  wire [27:0] shiftleft2_1_ins_index_2;
  wire [31:0] bit_extender_1_out, bit_extender_2_out, bit_extender_3_out, jumpaddressshift_1_targetaddress,
       mips_alu_1_p5, multiplexer_1_out, multiplexer_5_out, multiplexer_6_out, multiplexer_7_out,
       multiplexer_10_out, multiplexer_12_out;

  Multiplexer #(.select(2), .width(32), .enable("false")) multiplexer_1 (
    .in0(Rs), .in1(RegExMem), .in2(RegMemWb), .out(multiplexer_1_out), .sel(FwdA));  // open: in3
  Multiplexer #(.select(2), .width(32), .enable("false")) multiplexer_2 (
    .in0(Rt), .in1(RegExMem), .in2(RegMemWb), .out(Rt_2), .sel(FwdB));  // open: in3
  not not_1 (not_1_out, Stall);
  PCPlus4 pcplus4_1 (.PC(PC_4), .PCplus4(PC_4_2));
  Multiplexer #(.width(5), .enable("false")) multiplexer_3 (
    .in0(Sa), .in1(multiplexer_1_out[4:0]), .out(multiplexer_3_out), .sel(VS));
  Multiplexer #(.width(5), .enable("false")) multiplexer_4 (
    .in0(multiplexer_3_out), .in1(5'b10000), .out(multiplexer_4_out), .sel(Lui));
  assign bit_extender_1_out = {{16{1'b0}}, Imm};  // Bit_Extender bit_extender_1
  Multiplexer #(.width(32), .enable("false")) multiplexer_5 (
    .in0(bit_extender_1_out), .in1(bit_extender_2_out), .out(multiplexer_5_out), .sel(SignExt));
  assign bit_extender_2_out = {{16{Imm[15]}}, Imm};  // Bit_Extender bit_extender_2
  Multiplexer #(.width(32), .enable("false")) multiplexer_6 (
    .in0(Rt_2), .in1(multiplexer_5_out), .out(multiplexer_6_out), .sel(UseImm));
  Comparator comparator_1 (
    .A(multiplexer_1_out), .B(multiplexer_6_out), .Comp(CompOp), .Sign(Signed), .Branch(Branch),
    .Result(comparator_1_result));
  ShiftLeft2 shiftleft2_1 (.Ins_index(Ins_Index), .Ins_index_2(shiftleft2_1_ins_index_2));
  JumpAddressShift jumpaddressshift_1 (
    .Ins_IndShifted(shiftleft2_1_ins_index_2), .DelaySlotUppers(DelaySlot[31:28]),
    .TargetAddress(jumpaddressshift_1_targetaddress));
  Multiplexer #(.width(32), .enable("false")) multiplexer_7 (
    .in0(multiplexer_1_out), .in1({32{1'b0}}), .out(multiplexer_7_out), .sel(Move));
  // Mips_ALU mips_alu_1: pin names not known; wires that end beside it: multiplexer_7_out, multiplexer_6_out, ALUOp, multiplexer_4_out, mips_alu_1_p5
  assign bit_extender_3_out = {{31{1'b0}}, comparator_1_result};  // Bit_Extender bit_extender_3
  Multiplexer #(.width(32), .enable("false")) multiplexer_8 (
    .in0(jumpaddressshift_1_targetaddress), .in1(Rs), .out(JumpAddress), .sel(JumpReg));
  // Probe on mips_alu_1_p5
  Multiplexer #(.width(5), .enable("false")) multiplexer_9 (
    .in0(AddressRd), .in1({5{1'b1}}), .out(AddressRd_2), .sel(RetRegAddress));
  LastBit lastbit_1 (.In(mips_alu_1_p5), .Out(lastbit_1_out));
  Multiplexer #(.width(32), .enable("false")) multiplexer_10 (
    .in0(mips_alu_1_p5), .in1(bit_extender_3_out), .out(multiplexer_10_out), .sel(Comp));
  Multiplexer #(.enable("false")) multiplexer_11 (
    .in0(RegWrite), .in1(lastbit_1_out), .out(multiplexer_11_out), .sel(Move));
  and and_1 (RegWrite_2, multiplexer_11_out, not_1_out);
  Multiplexer #(.width(32), .enable("false")) multiplexer_12 (
    .in0(multiplexer_10_out), .in1(multiplexer_1_out), .out(multiplexer_12_out), .sel(Move));
  Multiplexer #(.width(32), .enable("false")) multiplexer_13 (
    .in0(multiplexer_12_out), .in1(PC_4_2), .out(OutputToStoreReg), .sel(StoreReturn));

  assign Jump_2 = Jump;
  assign Signed_2 = Signed;
endmodule

module EX_MEM (
  input  [31:0] JumpAddress,
  input  RegWrite,
  input  [31:0] OutputToStoreReg,
  input  Signed,
  input  [4:0] RdAddress,
  input  [31:0] PC_4,
  input  [31:0] Rt,
  input  Clock,
  input  Reset,
  output [31:0] JumpAddress_2,
  output RegWrite_2,
  output [31:0] OutputToStoreRegOut,
  output Signed_2,
  output [4:0] RdAddress_2,
  output [31:0] PC_4_2,
  output [31:0] Rt_2
);

  Register #(.width(32)) register_1 (.D(JumpAddress), .Q(JumpAddress_2), .clk(Clock), .clr(Reset));  // open: en
  Register #(.width(1)) register_2 (.D(RegWrite), .Q(RegWrite_2), .clk(Clock), .clr(Reset));  // open: en
  Register #(.width(32)) register_3 (
    .D(OutputToStoreReg), .Q(OutputToStoreRegOut), .clk(Clock), .clr(Reset));  // open: en
  Register #(.width(1)) register_4 (.D(Signed), .Q(Signed_2), .clk(Clock), .clr(Reset));  // open: en
  Register #(.width(5)) register_5 (.D(RdAddress), .Q(RdAddress_2), .clk(Clock), .clr(Reset));  // open: en
  Register #(.width(32)) register_6 (.D(PC_4), .Q(PC_4_2), .clk(Clock), .clr(Reset));  // open: en
  Register #(.width(32)) register_7 (.D(Rt), .Q(Rt_2), .clk(Clock), .clr(Clock));  // open: en
endmodule

module MEM (
  input  [31:0] JumpAddress,
  input  RegWrite,
  input  [31:0] OutputToStoreReg,
  input  Signed,
  input  [4:0] RdAddress,
  input  [31:0] PC_4,
  input  [31:0] Rt,
  input  MemSize,
  input  MemRead,
  input  MemWrite,
  input  MemToReg,
  output RegWrite_2,
  output [31:0] OutputToStoreRegOut,
  output [4:0] RdAddress_2,
  output [31:0] PC_4_2
);

  wire clock_1_out;
  wire [3:0] last2bitstoselects_1_s0, multiplexer_1_out;
  wire [7:0] multiplexer_2_out;
  wire [31:0] bit_extender_1_out, bit_extender_2_out, mips_ram_1_p7, multiplexer_3_out, multiplexer_4_out;

  Last2BitsToSelects last2bitstoselects_1 (
    .B1(OutputToStoreReg[0]), .B0(OutputToStoreReg[1]), .S0(last2bitstoselects_1_s0[0]),
    .S1(last2bitstoselects_1_s0[1]), .S3(last2bitstoselects_1_s0[2]), .S4(last2bitstoselects_1_s0[3]));
  Multiplexer #(.width(4), .enable("false")) multiplexer_1 (
    .in0(4'b0000), .in1(last2bitstoselects_1_s0), .out(multiplexer_1_out), .sel(MemSize));
  Clock clock_1 (.out(clock_1_out));
  // MIPS_RAM mips_ram_1: pin names not known; wires that end beside it: OutputToStoreReg[25:2], Rt, MemWrite, multiplexer_1_out, clock_1_out, MemRead, mips_ram_1_p7
  Multiplexer #(.select(2), .width(8), .enable("false")) multiplexer_2 (
    .in0(mips_ram_1_p7[7:0]), .in1(mips_ram_1_p7[15:8]), .in2(mips_ram_1_p7[23:16]),
    .in3(mips_ram_1_p7[31:24]), .out(multiplexer_2_out), .sel(OutputToStoreReg[1:0]));
  assign bit_extender_1_out = {{24{1'b0}}, multiplexer_2_out};  // Bit_Extender bit_extender_1
  assign bit_extender_2_out = {{24{multiplexer_2_out[7]}}, multiplexer_2_out};  // Bit_Extender bit_extender_2
  Multiplexer #(.width(32), .enable("false")) multiplexer_3 (
    .in0(bit_extender_1_out), .in1(bit_extender_2_out), .out(multiplexer_3_out), .sel(Signed));
  Multiplexer #(.width(32), .enable("false")) multiplexer_4 (
    .in0(mips_ram_1_p7), .in1(multiplexer_3_out), .out(multiplexer_4_out), .sel(MemSize));
  Multiplexer #(.width(32), .enable("false")) multiplexer_5 (
    .in0(OutputToStoreReg), .in1(multiplexer_4_out), .out(OutputToStoreRegOut), .sel(MemToReg));

  assign PC_4_2 = PC_4;
  assign RdAddress_2 = RdAddress;
  assign RegWrite_2 = RegWrite;
endmodule

module MEM_WB (
  input  RegWrite,
  input  [31:0] OutputToStoreReg,
  input  [4:0] RdAddress,
  input  [31:0] PC_4,
  input  Clock,
  input  Reset,
  output RegWrite_2,
  output [31:0] OutputToStoreRegOut,
  output [4:0] RdAddress_2,
  output [31:0] PC_4Out
);

  Register #(.width(1)) register_1 (.D(RegWrite), .Q(RegWrite_2), .clk(Clock), .clr(Reset));  // open: en
  Register #(.width(32)) register_2 (
    .D(OutputToStoreReg), .Q(OutputToStoreRegOut), .clk(Clock), .clr(Reset));  // open: en
  Register #(.width(5)) register_3 (.D(RdAddress), .Q(RdAddress_2), .clk(Clock), .clr(Reset));  // open: en
  Register #(.width(32)) register_4 (.D(PC_4), .Q(PC_4Out), .clk(Clock), .clr(Reset));  // open: en
endmodule

module DecodingLogic (
  input  Bit5,
  input  Bit4,
  input  Bit3,
  input  Bit2,
  input  Bit1,
  input  Bit0,
  input  Rtype,
  output RegDst,
  output RegWrite,
  output ALUSrc,
  output ALUOp3,
  output ALUOp2,
  output ALUOp1,
  output ALUOp0,
  output SignExt,
  output Move,
  output VS
);

  wire and_1_out, and_2_out, and_3_out, and_4_out, and_5_out, and_6_out, and_7_out, and_8_out, and_9_out,
       and_10_out, and_11_out, and_12_out, and_13_out, and_14_out, and_15_out, and_16_out, and_17_out,
       and_18_out, and_19_out, and_20_out, and_21_out, and_22_out, and_23_out, and_24_out, and_25_out,
       and_26_out, and_27_out, and_28_out, and_29_out, and_30_out, and_31_out, and_32_out, and_33_out,
       and_34_out, and_35_out, and_36_out, and_37_out, and_38_out, and_39_out, and_40_out, and_41_out,
       and_42_out, and_43_out, and_44_out, and_45_out, and_46_out, and_47_out, and_48_out, and_49_out,
       and_50_out, and_51_out, and_52_out, and_53_out, and_54_out, and_55_out, and_56_out, and_57_out,
       and_58_out, and_59_out, not_1_out, not_2_out, not_3_out, not_4_out, not_5_out, not_6_out, not_7_out,
       not_8_out, not_9_out, not_10_out, not_11_out, not_12_out, not_13_out, not_14_out, not_15_out,
       not_16_out, not_17_out, not_18_out, not_19_out, not_20_out, not_21_out, not_22_out, not_23_out,
       not_24_out, not_25_out, not_26_out, not_27_out, not_28_out, not_29_out, not_30_out, not_31_out,
       not_32_out, not_33_out, not_34_out, not_35_out, not_36_out, not_37_out, not_38_out, not_39_out,
       not_40_out, not_41_out, not_42_out, not_43_out, not_44_out, not_45_out, not_46_out, not_47_out,
       not_48_out, not_49_out, not_50_out, not_51_out, not_52_out, not_53_out, not_54_out, not_55_out,
       not_56_out, not_57_out, not_58_out, not_59_out, not_60_out, not_61_out, not_62_out, not_63_out,
       not_64_out, not_65_out, not_66_out, not_67_out, not_68_out, not_69_out, not_70_out, not_71_out,
       not_72_out, not_73_out, not_74_out, not_75_out, not_76_out, not_77_out, not_78_out, not_79_out,
       not_80_out, not_81_out, not_82_out, not_83_out, not_84_out, not_85_out, not_86_out, not_87_out,
       not_88_out, not_89_out, not_90_out, not_91_out, not_92_out, not_93_out, not_94_out, not_95_out,
       not_96_out, not_97_out, not_98_out, not_99_out, not_100_out, not_101_out, not_102_out, not_103_out,
       not_104_out, not_105_out, not_106_out, not_107_out, not_108_out, not_109_out, not_110_out,
       not_111_out, not_112_out, not_113_out, not_114_out, not_115_out, not_116_out, not_117_out,
       not_118_out, not_119_out, not_120_out, not_121_out, not_122_out, not_123_out, not_124_out,
       not_125_out, not_126_out, not_127_out, not_128_out, not_129_out, not_130_out, not_131_out,
       not_132_out, not_133_out, not_134_out, not_135_out, not_136_out, not_137_out, not_138_out,
       not_139_out, not_140_out, not_141_out, not_142_out, not_143_out, not_144_out, not_145_out,
       not_146_out, not_147_out, not_148_out, not_149_out, not_150_out, not_151_out, not_152_out,
       not_153_out, not_154_out, not_155_out, not_156_out;

  not not_1 (not_1_out, Bit5);
  not not_2 (not_2_out, Bit3);
  not not_3 (not_3_out, Bit0);
  not not_4 (not_4_out, Bit5);
  not not_5 (not_5_out, Bit3);
  not not_6 (not_6_out, Bit4);
  not not_7 (not_7_out, Bit3);
  not not_8 (not_8_out, Bit0);
  not not_9 (not_9_out, Bit4);
  not not_10 (not_10_out, Bit2);
  not not_11 (not_11_out, Bit5);
  not not_12 (not_12_out, Bit4);
  not not_13 (not_13_out, Bit3);
  not not_14 (not_14_out, Bit5);
  not not_15 (not_15_out, Bit3);
  not not_16 (not_16_out, Bit0);
  not not_17 (not_17_out, Bit5);
  not not_18 (not_18_out, Bit3);
  not not_19 (not_19_out, Bit4);
  not not_20 (not_20_out, Bit3);
  not not_21 (not_21_out, Bit2);
  not not_22 (not_22_out, Bit4);
  not not_23 (not_23_out, Bit3);
  not not_24 (not_24_out, Bit0);
  not not_25 (not_25_out, Bit5);
  not not_26 (not_26_out, Bit2);
  not not_27 (not_27_out, Bit5);
  not not_28 (not_28_out, Bit2);
  not not_29 (not_29_out, Bit4);
  not not_30 (not_30_out, Bit2);
  not not_31 (not_31_out, Bit5);
  not not_32 (not_32_out, Rtype);
  not not_33 (not_33_out, Bit4);
  not not_34 (not_34_out, Bit3);
  not not_35 (not_35_out, Bit1);
  not not_36 (not_36_out, Bit0);
  not not_37 (not_37_out, Rtype);
  not not_38 (not_38_out, Bit4);
  not not_39 (not_39_out, Bit3);
  not not_40 (not_40_out, Bit5);
  not not_41 (not_41_out, Rtype);
  not not_42 (not_42_out, Bit5);
  not not_43 (not_43_out, Rtype);
  not not_44 (not_44_out, Bit5);
  not not_45 (not_45_out, Rtype);
  not not_46 (not_46_out, Bit4);
  not not_47 (not_47_out, Bit3);
  not not_48 (not_48_out, Bit1);
  not not_49 (not_49_out, Bit0);
  not not_50 (not_50_out, Rtype);
  not not_51 (not_51_out, Bit4);
  not not_52 (not_52_out, Bit2);
  not not_53 (not_53_out, Bit1);
  not not_54 (not_54_out, Bit0);
  not not_55 (not_55_out, Rtype);
  not not_56 (not_56_out, Bit4);
  not not_57 (not_57_out, Bit2);
  not not_58 (not_58_out, Rtype);
  not not_59 (not_59_out, Bit5);
  not not_60 (not_60_out, Bit0);
  not not_61 (not_61_out, Rtype);
  not not_62 (not_62_out, Bit4);
  not not_63 (not_63_out, Bit2);
  not not_64 (not_64_out, Bit5);
  not not_65 (not_65_out, Bit1);
  not not_66 (not_66_out, Rtype);
  not not_67 (not_67_out, Bit5);
  not not_68 (not_68_out, Bit0);
  not not_69 (not_69_out, Bit5);
  not not_70 (not_70_out, Bit4);
  not not_71 (not_71_out, Bit3);
  not not_72 (not_72_out, Bit5);
  not not_73 (not_73_out, Bit3);
  not not_74 (not_74_out, Bit4);
  not not_75 (not_75_out, Bit3);
  not not_76 (not_76_out, Bit4);
  not not_77 (not_77_out, Bit3);
  not not_78 (not_78_out, Bit5);
  not not_79 (not_79_out, Bit0);
  not not_80 (not_80_out, Rtype);
  not not_81 (not_81_out, Bit5);
  not not_82 (not_82_out, Bit3);
  not not_83 (not_83_out, Bit5);
  not not_84 (not_84_out, Bit1);
  not not_85 (not_85_out, Rtype);
  not not_86 (not_86_out, Bit5);
  not not_87 (not_87_out, Bit2);
  not not_88 (not_88_out, Bit5);
  not not_89 (not_89_out, Bit2);
  not not_90 (not_90_out, Bit1);
  not not_91 (not_91_out, Bit5);
  not not_92 (not_92_out, Bit1);
  not not_93 (not_93_out, Bit5);
  not not_94 (not_94_out, Bit4);
  not not_95 (not_95_out, Bit3);
  not not_96 (not_96_out, Bit1);
  not not_97 (not_97_out, Bit0);
  not not_98 (not_98_out, Rtype);
  not not_99 (not_99_out, Bit4);
  not not_100 (not_100_out, Bit2);
  not not_101 (not_101_out, Bit1);
  not not_102 (not_102_out, Bit0);
  not not_103 (not_103_out, Rtype);
  not not_104 (not_104_out, Bit4);
  not not_105 (not_105_out, Bit3);
  not not_106 (not_106_out, Bit4);
  not not_107 (not_107_out, Bit2);
  not not_108 (not_108_out, Bit5);
  not not_109 (not_109_out, Bit4);
  not not_110 (not_110_out, Bit3);
  not not_111 (not_111_out, Bit2);
  not not_112 (not_112_out, Bit1);
  not not_113 (not_113_out, Bit0);
  not not_114 (not_114_out, Bit5);
  not not_115 (not_115_out, Bit3);
  not not_116 (not_116_out, Bit5);
  not not_117 (not_117_out, Bit4);
  not not_118 (not_118_out, Bit2);
  not not_119 (not_119_out, Bit5);
  not not_120 (not_120_out, Bit3);
  not not_121 (not_121_out, Bit5);
  not not_122 (not_122_out, Bit4);
  not not_123 (not_123_out, Bit2);
  not not_124 (not_124_out, Rtype);
  not not_125 (not_125_out, Bit5);
  not not_126 (not_126_out, Bit4);
  not not_127 (not_127_out, Bit2);
  not not_128 (not_128_out, Rtype);
  not not_129 (not_129_out, Bit4);
  not not_130 (not_130_out, Bit3);
  not not_131 (not_131_out, Bit1);
  not not_132 (not_132_out, Bit0);
  not not_133 (not_133_out, Rtype);
  not not_134 (not_134_out, Bit4);
  not not_135 (not_135_out, Bit2);
  not not_136 (not_136_out, Bit1);
  not not_137 (not_137_out, Bit0);
  not not_138 (not_138_out, Rtype);
  not not_139 (not_139_out, Bit4);
  not not_140 (not_140_out, Bit2);
  not not_141 (not_141_out, Rtype);
  not not_142 (not_142_out, Bit5);
  not not_143 (not_143_out, Bit2);
  not not_144 (not_144_out, Bit5);
  not not_145 (not_145_out, Bit4);
  not not_146 (not_146_out, Bit3);
  not not_147 (not_147_out, Bit0);
  not not_148 (not_148_out, Bit4);
  not not_149 (not_149_out, Bit3);
  not not_150 (not_150_out, Bit5);
  not not_151 (not_151_out, Bit3);
  not not_152 (not_152_out, Bit4);
  not not_153 (not_153_out, Bit3);
  and and_1 (and_1_out, not_1_out, not_2_out, not_3_out, Rtype);
  and and_2 (and_2_out, not_4_out, not_5_out, Bit1, Rtype);
  and and_3 (and_3_out, not_6_out, not_7_out, Bit2, not_8_out, Rtype);
  and and_4 (and_4_out, not_9_out, Bit3, not_10_out, Bit1, Rtype);
  and and_5 (and_5_out, not_11_out, Bit4, Rtype);
  and and_6 (and_6_out, Bit5, not_12_out, not_13_out, Bit0, Rtype);
  and and_7 (and_7_out, not_14_out, not_15_out, not_16_out, Rtype);
  and and_8 (and_8_out, not_17_out, not_18_out, Bit1, Rtype);
  and and_9 (and_9_out, not_19_out, not_20_out, not_21_out, Bit1, Bit0);
  and and_10 (and_10_out, not_22_out, not_23_out, Bit2, not_24_out, Rtype);
  and and_11 (and_11_out, not_25_out, Bit3, not_26_out, Bit0);
  and and_12 (and_12_out, not_27_out, Bit3, not_28_out, Bit1);
  and and_13 (and_13_out, not_29_out, Bit3, not_30_out, Bit1, Rtype);
  and and_14 (and_14_out, not_31_out, Bit3, Bit2, not_32_out);
  not not_154 (not_154_out, Bit5);
  and and_15 (and_15_out, not_154_out, Bit4);
  and and_16 (and_16_out, Bit5, not_33_out, not_34_out, not_35_out, not_36_out, not_37_out);
  and and_17 (and_17_out, Bit5, not_38_out, not_39_out, Bit0, Rtype);
  and and_18 (and_18_out, not_40_out, Bit3, Bit0, not_41_out);
  and and_19 (and_19_out, not_42_out, Bit3, Bit1, not_43_out);
  and and_20 (and_20_out, not_44_out, Bit3, Bit2, not_45_out);
  not not_155 (not_155_out, Bit5);
  and and_21 (and_21_out, not_155_out, Bit4, not_156_out);
  not not_156 (not_156_out, Rtype);
  and and_22 (and_22_out, Bit5, not_46_out, not_47_out, not_48_out, not_49_out, not_50_out);
  and and_23 (and_23_out, Bit5, not_51_out, not_52_out, not_53_out, not_54_out, not_55_out);
  and and_24 (and_24_out, Bit5, not_56_out, not_57_out, Bit1, Bit0, not_58_out);
  and and_25 (and_25_out, not_59_out, Bit3, Bit1, not_60_out, not_61_out);
  and and_26 (and_26_out, not_62_out, Bit3, not_63_out, Bit1, Rtype);
  and and_27 (and_27_out, not_64_out, Bit3, Bit2, not_65_out, not_66_out);
  and and_28 (and_28_out, not_67_out, Bit4, Bit3, not_68_out);
  and and_29 (and_29_out, not_69_out, Bit4, Bit3, Rtype);
  and and_30 (and_30_out, Bit5, not_70_out, not_71_out, Bit2, Rtype);
  and and_31 (and_31_out, not_72_out, not_73_out, Bit1, Rtype);
  and and_32 (and_32_out, not_74_out, not_75_out, Bit1, Bit0, Rtype);
  and and_33 (and_33_out, not_76_out, not_77_out, Bit2, Bit1, Rtype);
  and and_34 (and_34_out, not_78_out, Bit3, Bit1, not_79_out, not_80_out);
  and and_35 (and_35_out, not_81_out, Bit4, not_82_out, Bit1);
  and and_36 (and_36_out, not_83_out, Bit3, not_84_out, Bit0, not_85_out);
  and and_37 (and_37_out, not_86_out, Bit3, not_87_out, Bit1, Bit0, Rtype);
  and and_38 (and_38_out, not_88_out, Bit4, not_89_out, not_90_out);
  and and_39 (and_39_out, not_91_out, Bit4, not_92_out, Bit0);
  and and_40 (and_40_out, not_93_out, Bit4, Bit3, Bit0, Rtype);
  and and_41 (and_41_out, Bit5, not_94_out, not_95_out, not_96_out, not_97_out, not_98_out);
  and and_42 (and_42_out, Bit5, not_99_out, not_100_out, not_101_out, not_102_out, not_103_out);
  and and_43 (and_43_out, Bit5, not_104_out, not_105_out, Bit0, Rtype);
  and and_44 (and_44_out, Bit5, not_106_out, not_107_out, Bit1, Bit0);
  and and_45 (and_45_out, not_108_out, not_109_out, not_110_out, not_111_out, not_112_out, not_113_out, Rtype);
  and and_46 (and_46_out, not_114_out, not_115_out, Bit1, Bit0, Rtype);
  and and_47 (and_47_out, not_116_out, not_117_out, Bit3, not_118_out, Bit1, Rtype);
  and and_48 (and_48_out, not_119_out, Bit4, not_120_out, Bit0);
  and and_49 (and_49_out, not_121_out, not_122_out, Bit3, not_123_out, Bit0, not_124_out);
  and and_50 (and_50_out, not_125_out, not_126_out, Bit3, not_127_out, Bit1, not_128_out);
  and and_51 (and_51_out, Bit5, not_129_out, not_130_out, not_131_out, not_132_out, not_133_out);
  and and_52 (and_52_out, Bit5, not_134_out, not_135_out, not_136_out, not_137_out, not_138_out);
  and and_53 (and_53_out, Bit5, not_139_out, not_140_out, Bit1, Bit0, not_141_out);
  and and_54 (and_54_out, not_142_out, Bit3, not_143_out, Bit1, Rtype);
  and and_55 (and_55_out, not_144_out, Bit4, Bit3, Rtype);
  and and_56 (and_56_out, not_145_out, not_146_out, Bit2, not_147_out, Rtype);
  and and_57 (and_57_out, not_148_out, not_149_out, Bit2, Bit1, Rtype);
  and and_58 (and_58_out, not_150_out, Bit4, not_151_out, Bit2);
  and and_59 (and_59_out, Bit5, not_152_out, not_153_out, Bit2, Rtype);
  or or_1 (RegDst, and_1_out, and_2_out, and_3_out, and_4_out, and_5_out, and_6_out);
  or or_2 (ALUOp3, and_25_out, and_26_out, and_27_out, and_28_out, and_29_out, and_30_out);
  or or_3 (ALUOp2, and_31_out, and_32_out, and_33_out, and_34_out, and_35_out);
  or or_4 (ALUOp0, and_45_out, and_46_out, and_47_out, and_48_out);
  or or_5 (SignExt, and_49_out, and_50_out, and_51_out, and_52_out, and_53_out);
  or or_6 (Move, and_54_out, and_55_out);
  or or_7 (VS, and_56_out, and_57_out, and_58_out, and_59_out);
  or or_8 (RegWrite, and_7_out, and_8_out, and_9_out, and_10_out, and_11_out, and_12_out, and_13_out, and_14_out, and_15_out, and_16_out, and_17_out);
  or or_9 (ALUSrc, and_18_out, and_19_out, and_20_out, and_21_out, and_22_out, and_23_out, and_24_out);
  or or_10 (ALUOp1, and_36_out, and_37_out, and_38_out, and_39_out, and_40_out, and_41_out, and_42_out, and_43_out, and_44_out);
endmodule

module PCPlus4 (
  input  [31:0] PC,
  output [31:0] PCplus4
);

  // Incrementer incrementer_1: pin names not known; wires that end beside it: PC[31:2], PCplus4[31:2]

  assign PCplus4[1:0] = PC[1:0];
endmodule

module LastBit (
  input  [31:0] In,
  output Out
);


  assign Out = In[0];
endmodule

module DataHazDetect (
  input  [4:0] Ra,
  input  [4:0] IdEx,
  input  [4:0] ExMem,
  input  [4:0] MemWb,
  input  [4:0] Rb,
  output DataHaz
);

  wire and_1_out, and_2_out, equator5_1_eq, equator5_2_eq, equator5_3_eq, equator5_4_eq, equator5_5_eq,
       equator5_6_eq, or_1_out, or_2_out, or_3_out, or_4_out;

  or or_1 (or_1_out, Ra[0], Ra[1], Ra[2], Ra[3], Ra[4]);
  Equator5 equator5_1 (.A(Ra), .B(IdEx), .Eq(equator5_1_eq));
  Equator5 equator5_2 (.A(Ra), .B(ExMem), .Eq(equator5_2_eq));
  Equator5 equator5_3 (.A(Ra), .B(MemWb), .Eq(equator5_3_eq));
  or or_2 (or_2_out, Rb[0], Rb[1], Rb[2], Rb[3], Rb[4]);
  Equator5 equator5_4 (.A(Rb), .B(MemWb), .Eq(equator5_4_eq));
  Equator5 equator5_5 (.A(Rb), .B(ExMem), .Eq(equator5_5_eq));
  Equator5 equator5_6 (.A(Rb), .B(IdEx), .Eq(equator5_6_eq));
  and and_1 (and_1_out, or_1_out, or_3_out);
  or or_3 (or_3_out, equator5_1_eq, equator5_2_eq, equator5_3_eq);
  and and_2 (and_2_out, or_2_out, or_4_out);
  or or_4 (or_4_out, equator5_4_eq, equator5_5_eq, equator5_6_eq);
  or or_5 (DataHaz, and_1_out, and_2_out);
endmodule

module ForwardExMem (
  input  WE,
  input  [4:0] Rd,
  input  [4:0] Ra_Rb,
  output Forward
);

  wire equator5_1_eq, or_1_out;

  or or_1 (or_1_out, Rd[0], Rd[1], Rd[2], Rd[3], Rd[4]);
  Equator5 equator5_1 (.A(Ra_Rb), .B(Rd), .Eq(equator5_1_eq));
  and and_1 (Forward, WE, or_1_out, equator5_1_eq);
endmodule

module ForwardMemWb (
  input  WE,
  input  [4:0] Rd,
  input  [4:0] Ra_Rb,
  input  WE0,
  input  [4:0] Rd0,
  output Forward
);

  wire equator5_1_eq, forwardexmem_1_forward, not_1_out, or_1_out;

  or or_1 (or_1_out, Rd[0], Rd[1], Rd[2], Rd[3], Rd[4]);
  Equator5 equator5_1 (.A(Rd), .B(Ra_Rb), .Eq(equator5_1_eq));
  ForwardExMem forwardexmem_1 (.WE(WE0), .Rd(Rd0), .Ra_Rb(Ra_Rb), .Forward(forwardexmem_1_forward));
  not not_1 (not_1_out, forwardexmem_1_forward);
  and and_1 (Forward, WE, or_1_out, equator5_1_eq, not_1_out);
endmodule

module BypassWb (
  input  [4:0] Ra,
  input  [4:0] Rb,
  input  [4:0] Rd,
  input  Writing,
  output Bypass
);

  wire equator5_1_eq, equator5_2_eq, or_1_out;

  Equator5 equator5_1 (.A(Ra), .B(Rd), .Eq(equator5_1_eq));
  Equator5 equator5_2 (.A(Rb), .B(Rd), .Eq(equator5_2_eq));
  or or_1 (or_1_out, equator5_1_eq, equator5_2_eq);
  and and_1 (Bypass, or_1_out, Writing);
endmodule

module NopDecode (
  input  [5:0] Opcode,
  output Out
);

  wire and_1_out, and_2_out, and_3_out, and_4_out, and_5_out, and_6_out, and_7_out, not_1_out, not_2_out,
       not_3_out, not_4_out, not_5_out, not_6_out, not_7_out, not_8_out, not_9_out, not_10_out, not_11_out,
       not_12_out, not_13_out, not_14_out, not_15_out, not_16_out, not_17_out, not_18_out, not_19_out,
       not_20_out, not_21_out, not_22_out, not_23_out, not_24_out, not_25_out, not_26_out;

  not not_1 (not_1_out, Opcode[5]);
  not not_2 (not_2_out, Opcode[4]);
  not not_3 (not_3_out, Opcode[3]);
  not not_4 (not_4_out, Opcode[1]);
  not not_5 (not_5_out, Opcode[5]);
  not not_6 (not_6_out, Opcode[4]);
  not not_7 (not_7_out, Opcode[3]);
  not not_8 (not_8_out, Opcode[2]);
  not not_9 (not_9_out, Opcode[5]);
  not not_10 (not_10_out, Opcode[4]);
  not not_11 (not_11_out, Opcode[3]);
  not not_12 (not_12_out, Opcode[0]);
  not not_13 (not_13_out, Opcode[4]);
  not not_14 (not_14_out, Opcode[3]);
  not not_15 (not_15_out, Opcode[1]);
  not not_16 (not_16_out, Opcode[0]);
  not not_17 (not_17_out, Opcode[4]);
  not not_18 (not_18_out, Opcode[2]);
  not not_19 (not_19_out, Opcode[1]);
  not not_20 (not_20_out, Opcode[0]);
  not not_21 (not_21_out, Opcode[4]);
  not not_22 (not_22_out, Opcode[3]);
  not not_23 (not_23_out, Opcode[1]);
  not not_24 (not_24_out, Opcode[0]);
  not not_25 (not_25_out, Opcode[4]);
  not not_26 (not_26_out, Opcode[2]);
  and and_1 (and_1_out, not_1_out, not_2_out, not_3_out, not_4_out, Opcode[0]);
  and and_2 (and_2_out, not_5_out, not_6_out, not_7_out, not_8_out, Opcode[1]);
  and and_3 (and_3_out, not_9_out, not_10_out, not_11_out, Opcode[2], not_12_out);
  and and_4 (and_4_out, not_13_out, not_14_out, Opcode[2], not_15_out, not_16_out);
  and and_5 (and_5_out, not_17_out, Opcode[3], not_18_out, not_19_out, not_20_out);
  and and_6 (and_6_out, Opcode[5], not_21_out, not_22_out, not_23_out, not_24_out);
  and and_7 (and_7_out, Opcode[5], not_25_out, not_26_out, Opcode[1], Opcode[0]);
  or or_1 (Out, and_1_out, and_2_out, and_3_out, and_4_out, and_5_out, and_6_out, and_7_out);
endmodule

module Last2BitsToSelects (
  input  B1,
  input  B0,
  output S0,
  output S1,
  output S3,
  output S4
);

  wire not_1_out, not_2_out, not_3_out, not_4_out;

  and and_1 (S0, B1, B0);
  not not_1 (not_1_out, B0);
  not not_2 (not_2_out, B1);
  not not_3 (not_3_out, B1);
  not not_4 (not_4_out, B0);
  and and_2 (S1, B1, not_1_out);
  and and_3 (S3, not_2_out, B0);
  and and_4 (S4, not_3_out, not_4_out);
endmodule

module StallChecker (
  input  ID_EX_MemRead,
  input  [4:0] IF_ID_Rs,
  input  [4:0] ID_EX_Rt,
  input  [4:0] IF_ID_Rt,
  output Stall
);

  wire equator5_1_eq, equator5_2_eq;

  Equator5 equator5_1 (.A(IF_ID_Rs), .B(ID_EX_Rt), .Eq(equator5_1_eq));
  Equator5 equator5_2 (.A(ID_EX_Rt), .B(IF_ID_Rt), .Eq(equator5_2_eq));
  and and_1 (Stall, ID_EX_MemRead, equator5_1_eq, equator5_2_eq);
endmodule

module Comparator (
  input  [31:0] A,
  input  [31:0] B,
  input  Sign,
  input  [2:0] Comp,
  input  Branch,
  output Result
);

  wire and_1_out, and_2_out, and_3_out, and_4_out, and_5_out, comparator_1_eq, comparator_1_lt,
       comparator_2_eq, comparator_2_lt, multiplexer_1_out, multiplexer_2_out, multiplexer_3_out, or_1_out;

  Comparator_part #(.width(32), .mode("unsigned")) comparator_1 (
    .a(A), .b(B), .eq(comparator_1_eq), .lt(comparator_1_lt));  // open: gt
  Comparator_part #(.width(32)) comparator_2 (.a(A), .b(B), .eq(comparator_2_eq), .lt(comparator_2_lt));  // open: gt
  and and_1 (and_1_out, Comp[2], comparator_1_eq);
  and and_2 (and_2_out, Comp[2], comparator_2_eq);
  Multiplexer #(.enable("false")) multiplexer_1 (
    .in0(and_1_out), .in1(and_2_out), .out(multiplexer_1_out), .sel(or_1_out));
  or or_1 (or_1_out, Sign, Branch);
  and and_3 (and_3_out, comparator_1_lt, Comp[1]);
  and and_4 (and_4_out, comparator_2_lt, Comp[1]);
  Multiplexer #(.enable("false")) multiplexer_2 (
    .in0(and_3_out), .in1(and_4_out), .out(multiplexer_2_out), .sel(or_1_out));
  and and_5 (and_5_out, multiplexer_2_out, multiplexer_1_out);
  Multiplexer #(.select(2), .enable("false")) multiplexer_3 (
    .in0(multiplexer_2_out), .in1(multiplexer_1_out), .in2(and_5_out), .out(multiplexer_3_out),
    .sel(Comp[2:1]));  // open: in3
  xor xor_1 (Result, multiplexer_3_out, Comp[0]);
endmodule

module DecodingLogicComp (
  input  Bit5,
  input  Bit4,
  input  Bit3,
  input  Bit2,
  input  Bit1,
  input  Bit0,
  input  Rtype,
  output Comp2,
  output Comp1,
  output Comp0,
  output Signed,
  output Comp
);

  wire and_2_out, and_3_out, and_4_out, and_6_out, and_7_out, and_8_out, and_9_out, and_10_out, and_11_out,
       and_12_out, not_1_out, not_2_out, not_3_out, not_4_out, not_5_out, not_6_out, not_7_out, not_8_out,
       not_9_out, not_10_out, not_11_out, not_12_out, not_13_out, not_14_out, not_15_out, not_16_out,
       not_17_out, not_18_out, not_19_out, not_20_out, not_21_out, not_22_out, not_23_out, not_24_out,
       not_25_out, not_26_out, not_27_out, not_28_out, not_29_out, not_30_out, not_31_out, not_32_out,
       not_33_out, not_34_out, not_35_out, not_36_out, not_37_out, not_38_out, not_39_out, not_40_out,
       not_41_out, not_42_out, not_43_out, not_44_out;

  not not_1 (not_1_out, Bit5);
  not not_2 (not_2_out, Bit4);
  not not_3 (not_3_out, Bit3);
  not not_4 (not_4_out, Rtype);
  not not_5 (not_5_out, Bit5);
  not not_6 (not_6_out, Bit4);
  not not_7 (not_7_out, Bit3);
  not not_8 (not_8_out, Rtype);
  not not_9 (not_9_out, Bit5);
  not not_10 (not_10_out, Bit4);
  not not_11 (not_11_out, Bit2);
  not not_12 (not_12_out, Rtype);
  not not_13 (not_13_out, Bit4);
  not not_14 (not_14_out, Bit2);
  not not_15 (not_15_out, Bit5);
  not not_16 (not_16_out, Bit4);
  not not_17 (not_17_out, Bit3);
  not not_18 (not_18_out, Rtype);
  not not_19 (not_19_out, Bit5);
  not not_20 (not_20_out, Bit4);
  not not_21 (not_21_out, Bit2);
  not not_22 (not_22_out, Bit0);
  not not_23 (not_23_out, Rtype);
  not not_24 (not_24_out, Bit4);
  not not_25 (not_25_out, Bit3);
  not not_26 (not_26_out, Bit2);
  not not_27 (not_27_out, Bit1);
  not not_28 (not_28_out, Bit0);
  not not_29 (not_29_out, Rtype);
  not not_30 (not_30_out, Bit4);
  not not_31 (not_31_out, Bit3);
  not not_32 (not_32_out, Bit2);
  not not_33 (not_33_out, Rtype);
  not not_34 (not_34_out, Bit4);
  not not_35 (not_35_out, Bit2);
  not not_36 (not_36_out, Bit0);
  not not_37 (not_37_out, Bit5);
  not not_38 (not_38_out, Bit2);
  not not_39 (not_39_out, Rtype);
  not not_40 (not_40_out, Bit5);
  not not_41 (not_41_out, Bit2);
  not not_42 (not_42_out, Rtype);
  not not_43 (not_43_out, Bit4);
  not not_44 (not_44_out, Bit2);
  and and_1 (Comp2, not_1_out, not_2_out, not_3_out, Bit2, not_4_out);
  and and_2 (and_2_out, not_5_out, not_6_out, not_7_out, Bit2, Bit1, not_8_out);
  and and_3 (and_3_out, not_9_out, not_10_out, Bit3, not_11_out, Bit1, not_12_out);
  and and_4 (and_4_out, Bit5, not_13_out, Bit3, not_14_out, Bit1, Rtype);
  and and_5 (Comp0, not_15_out, not_16_out, not_17_out, Bit2, Bit0, not_18_out);
  and and_6 (and_6_out, not_19_out, not_20_out, Bit3, not_21_out, Bit1, not_22_out, not_23_out);
  and and_7 (and_7_out, Bit5, not_24_out, not_25_out, not_26_out, not_27_out, not_28_out, not_29_out);
  and and_8 (and_8_out, Bit5, not_30_out, not_31_out, not_32_out, Bit1, Bit0, not_33_out);
  and and_9 (and_9_out, Bit5, not_34_out, Bit3, not_35_out, Bit1, not_36_out, Rtype);
  and and_10 (and_10_out, not_37_out, Bit3, not_38_out, Bit1, not_39_out);
  and and_11 (and_11_out, not_40_out, Bit4, not_41_out, Bit1, not_42_out);
  and and_12 (and_12_out, Bit5, not_43_out, Bit3, not_44_out, Bit1, Rtype);
  or or_1 (Comp1, and_2_out, and_3_out, and_4_out);
  or or_2 (Signed, and_6_out, and_7_out, and_8_out, and_9_out);
  or or_3 (Comp, and_10_out, and_11_out, and_12_out);
endmodule

module Equator5 (
  input  [4:0] A,
  input  [4:0] B,
  output Eq
);

  wire [4:0] xor_1_out;

  assign xor_1_out = A ^ B;  // XOR_Gate xor_1, 5 bits wide
  nor nor_1 (Eq, xor_1_out[0], xor_1_out[1], xor_1_out[2], xor_1_out[3], xor_1_out[4]);
endmodule

module ShiftLeft2 (
  input  [25:0] Ins_index,
  output [27:0] Ins_index_2
);


  assign Ins_index_2 = {Ins_index, 2'b00};
endmodule

module DelaySlot (
  input  [31:0] Instruction,
  output [31:0] Instruction_2
);


  assign Instruction_2 = Instruction;
endmodule

module JumpAddressShift (
  input  [27:0] Ins_IndShifted,
  input  [3:0] DelaySlotUppers,
  output [31:0] TargetAddress
);


  assign TargetAddress = {DelaySlotUppers, Ins_IndShifted};
endmodule

module SelectBitCondenser (
  input  b3,
  input  b2,
  input  b1,
  input  b0,
  output O1,
  output O2
);

  wire not_1_out, not_2_out, not_3_out, not_4_out;

  not not_1 (not_1_out, b1);
  and and_1 (O1, not_1_out, not_2_out);
  not not_2 (not_2_out, b0);
  not not_3 (not_3_out, b2);
  and and_2 (O2, not_3_out, not_4_out);
  not not_4 (not_4_out, b0);
endmodule

module DecodingLogicLui (
  input  Bit5,
  input  Bit4,
  input  Bit3,
  input  Bit2,
  input  Bit1,
  input  Bit0,
  input  Rtype,
  output LUI
);

  wire not_1_out, not_2_out, not_3_out;

  not not_1 (not_1_out, Bit5);
  not not_2 (not_2_out, Bit4);
  not not_3 (not_3_out, Rtype);
  and and_1 (LUI, not_1_out, not_2_out, Bit3, Bit2, Bit1, Bit0, not_3_out);
endmodule

module DecodingLogicBranch (
  input  Bit5,
  input  Bit4,
  input  Bit3,
  input  Bit2,
  input  Bit1,
  input  Bit0,
  input  Rtype,
  input  REGIMM,
  output Branch
);

  wire and_1_out, and_2_out, not_1_out, not_2_out, not_3_out, not_4_out, not_5_out, not_6_out, not_7_out,
       not_8_out, not_9_out, not_10_out;

  not not_1 (not_1_out, Bit5);
  not not_2 (not_2_out, Bit4);
  not not_3 (not_3_out, Bit3);
  not not_4 (not_4_out, Bit2);
  not not_5 (not_5_out, Bit1);
  not not_6 (not_6_out, Bit5);
  not not_7 (not_7_out, Bit4);
  not not_8 (not_8_out, Bit3);
  not not_9 (not_9_out, Rtype);
  not not_10 (not_10_out, REGIMM);
  and and_1 (and_1_out, not_1_out, not_2_out, not_3_out, not_4_out, not_5_out, Bit0, REGIMM);
  and and_2 (and_2_out, not_6_out, not_7_out, not_8_out, Bit2, not_9_out, not_10_out);
  or or_1 (Branch, and_1_out, and_2_out);
endmodule

module DecodingREGIMM (
  input  Bit5,
  input  Bit4,
  input  Bit3,
  input  Bit2,
  input  Bit1,
  input  Bit0,
  input  Rtype,
  output REGIMM
);

  wire not_1_out, not_2_out, not_3_out, not_4_out, not_5_out, not_6_out;

  not not_1 (not_1_out, Bit5);
  not not_2 (not_2_out, Bit4);
  not not_3 (not_3_out, Bit3);
  not not_4 (not_4_out, Bit2);
  not not_5 (not_5_out, Bit1);
  not not_6 (not_6_out, Rtype);
  and and_1 (REGIMM, not_1_out, not_2_out, not_3_out, not_4_out, not_5_out, Bit0, not_6_out);
endmodule

module DecodingMem_Jumps (
  input  b5,
  input  b4,
  input  b3,
  input  b2,
  input  b1,
  input  b0,
  input  r,
  output MemRd,
  output MemW,
  output JumpReg,
  output MemToReg,
  output RetRegAdd,
  output StoreRet,
  output MemSize,
  output Jump
);

  wire and_1_out, and_2_out, and_3_out, and_4_out, and_5_out, and_6_out, not_1_out, not_2_out, not_3_out,
       not_4_out, not_5_out, not_6_out, not_7_out, not_8_out, not_9_out, not_10_out, not_11_out, not_12_out,
       not_13_out, not_14_out, not_15_out, not_16_out, not_17_out, not_21_out, not_22_out, not_23_out,
       not_24_out, not_25_out, not_26_out, not_27_out, not_28_out, not_29_out;

  not not_1 (not_1_out, b4);
  not not_2 (not_2_out, b3);
  not not_3 (not_3_out, b1);
  not not_4 (not_4_out, b0);
  not not_5 (not_5_out, r);
  not not_6 (not_6_out, b4);
  not not_7 (not_7_out, b3);
  not not_8 (not_8_out, b2);
  not not_9 (not_9_out, r);
  not not_10 (not_10_out, b4);
  not not_11 (not_11_out, b2);
  not not_12 (not_12_out, b1);
  not not_13 (not_13_out, b0);
  not not_14 (not_14_out, r);
  not not_15 (not_15_out, b4);
  not not_16 (not_16_out, b2);
  not not_17 (not_17_out, r);
  not not_18 (JumpReg, b1);
  not not_19 (RetRegAdd, b1);
  not not_20 (MemSize, b1);
  not not_21 (not_21_out, b5);
  not not_22 (not_22_out, b4);
  not not_23 (not_23_out, b3);
  not not_24 (not_24_out, b2);
  not not_25 (not_25_out, r);
  not not_26 (not_26_out, b5);
  not not_27 (not_27_out, b4);
  not not_28 (not_28_out, b2);
  not not_29 (not_29_out, b1);
  and and_1 (and_1_out, b5, not_1_out, not_2_out, not_3_out, not_4_out, not_5_out);
  and and_2 (and_2_out, b5, not_6_out, not_7_out, not_8_out, b1, b0, not_9_out);
  and and_3 (and_3_out, b5, not_10_out, b3, not_11_out, not_12_out, not_13_out, not_14_out);
  and and_4 (and_4_out, b5, not_15_out, b3, not_16_out, b1, b0, not_17_out);
  and and_5 (and_5_out, not_21_out, not_22_out, not_23_out, not_24_out, b1, not_25_out);
  and and_6 (and_6_out, not_26_out, not_27_out, b3, not_28_out, not_29_out, r);
  or or_1 (MemRd, and_1_out, and_2_out);
  or or_2 (MemW, and_3_out, and_4_out);
  or or_3 (Jump, and_5_out, and_6_out);

  assign MemToReg = 1'b0;
  assign StoreRet = 1'b0;
endmodule

module ID_EX2 (
  input  MemRead,
  input  MemWrite,
  input  JumpReg,
  input  MemToReg,
  input  RetRegAdd,
  input  StoreReturn,
  input  MemSize,
  input  Jump,
  input  Clock,
  input  Reset,
  output MemRead_2,
  output MemWrite_2,
  output JumpReg_2,
  output MemToReg_2,
  output RetRegAdd_2,
  output StoreReturn_2,
  output MemSize_2,
  output Jump_2
);

  Register #(.width(1)) register_1 (.D(MemRead), .Q(MemRead_2), .clk(Clock), .clr(Reset));  // open: en
  Register #(.width(1)) register_2 (.D(MemWrite), .Q(MemWrite_2), .clk(Clock), .clr(Reset));  // open: en
  Register #(.width(1)) register_3 (.D(JumpReg), .Q(JumpReg_2), .clk(Clock), .clr(Reset));  // open: en
  Register #(.width(1)) register_4 (.D(MemToReg), .Q(MemToReg_2), .clk(Clock), .clr(Reset));  // open: en
  Register #(.width(1)) register_5 (.D(RetRegAdd), .Q(RetRegAdd_2), .clk(Clock), .clr(Reset));  // open: en
  Register #(.width(1)) register_6 (.D(StoreReturn), .Q(StoreReturn_2), .clk(Clock), .clr(Reset));  // open: en
  Register #(.width(1)) register_7 (.D(MemSize), .Q(MemSize_2), .clk(Clock), .clr(Reset));  // open: en
  Register #(.width(1)) register_8 (.D(Jump), .Q(Jump_2), .clk(Clock), .clr(Reset));  // open: en
endmodule

module EX_MEM2 (
  input  MemToReg,
  input  MemWrite,
  input  MemRead,
  input  MemSize,
  input  Clock,
  input  Reset,
  output MemToReg_2,
  output MemWrite_2,
  output MemRead_2,
  output MemSize_2
);

  Register #(.width(1)) register_1 (.D(MemToReg), .Q(MemToReg_2), .clk(Clock), .clr(Reset));  // open: en
  Register #(.width(1)) register_2 (.D(MemWrite), .Q(MemWrite_2), .clk(Clock), .clr(Reset));  // open: en
  Register #(.width(1)) register_3 (.D(MemRead), .Q(MemRead_2), .clk(Clock), .clr(Reset));  // open: en
  Register #(.width(1)) register_4 (.D(MemSize), .Q(MemSize_2), .clk(Clock), .clr(Reset));  // open: en
endmodule
